// Logisim project 4_bit_processor.circ as structural Verilog
module _3_port_register_file (
  input  [3:0] Data_in,
  input  Enable,
  input  [1:0] select_out0,
  input  [1:0] Register_Select,
  input  Enable_2,
  input  [1:0] Select_Out1,
  input  RegWrite,
  input  Clear_Register,
  output [3:0] Out0,
  output [3:0] Out1
);

  wire and_1_out, Clock_out, decoder_1_out0, decoder_1_out1, decoder_1_out2, decoder_1_out3;
  wire [3:0] register_1_q, register_2_q, register_3_q, register_4_q;

  Decoder #(.select(2), .enable("false")) decoder_1 (
    .out0(decoder_1_out0), .out1(decoder_1_out1), .out2(decoder_1_out2), .out3(decoder_1_out3),
    .sel(Register_Select));
  Clock Clock (.out(Clock_out));
  and and_1 (and_1_out, Clock_out, RegWrite);
  Register #(.width(4)) register_1 (
    .D(Data_in), .en(decoder_1_out0), .Q(register_1_q), .clk(and_1_out), .clr(Clear_Register));
  Register #(.width(4)) register_2 (
    .D(Data_in), .en(decoder_1_out2), .Q(register_2_q), .clk(and_1_out), .clr(Clear_Register));
  Register #(.width(4)) register_3 (
    .D(Data_in), .en(decoder_1_out1), .Q(register_3_q), .clk(and_1_out), .clr(Clear_Register));
  Register #(.width(4)) register_4 (
    .D(Data_in), .en(decoder_1_out3), .Q(register_4_q), .clk(and_1_out), .clr(Clear_Register));
  Multiplexer #(.select(2), .width(4)) multiplexer_1 (
    .in0(register_1_q), .in1(register_3_q), .in2(register_2_q), .in3(register_4_q), .out(Out0),
    .sel(select_out0), .en(Enable));
  Multiplexer #(.select(2), .width(4)) multiplexer_2 (
    .in0(register_1_q), .in1(register_3_q), .in2(register_2_q), .in3(register_4_q), .out(Out1),
    .sel(Select_Out1), .en(Enable_2));
endmodule

module _4_Bit_ALU (
  input  [3:0] Input_0,
  input  [3:0] Input_1,
  input  [2:0] Function,
  output [3:0] Result,
  output Test_for_Output__beq
);

  wire [3:0] adder_1_out, and_1_out, and_2_out, divider_1_out, multiplier_1_out, odd_parity_1_out, or_1_out,
       shifter_1_out, subtractor_1_out;

  Adder #(.width(4)) adder_1 (.a(Input_0), .b(Input_1), .out(adder_1_out));  // open: cin, cout
  Subtractor #(.width(4)) subtractor_1 (.a(Input_0), .b(Input_1), .out(subtractor_1_out));  // open: bin, bout
  assign or_1_out = Input_0 | Input_1;  // OR_Gate or_1, 4 bits wide
  assign and_1_out = Input_0 & Input_1;  // AND_Gate and_1, 4 bits wide
  Multiplier #(.width(4)) multiplier_1 (.a(Input_0), .b(Input_1), .out(multiplier_1_out));  // open: cin, cout
  Divider #(.width(4)) divider_1 (.a(Input_0), .b(Input_1), .out(divider_1_out));  // open: upper, rem
  Shifter #(.width(4)) shifter_1 (.in(Input_0), .\dist (Input_1[1:0]), .out(shifter_1_out));
  assign odd_parity_1_out = Input_0 ^ Input_1;  // Odd_Parity odd_parity_1, 4 bits wide
  Multiplexer #(.select(3), .width(4)) multiplexer_1 (
    .in0(adder_1_out), .in1(subtractor_1_out), .in2(or_1_out), .in3(and_1_out), .in4(multiplier_1_out),
    .in5(divider_1_out), .in6(shifter_1_out), .in7(odd_parity_1_out), .out(Result), .sel(Function));  // open: en
  assign and_2_out = subtractor_1_out & 4'b1111;  // AND_Gate and_2, 4 bits wide
  not not_1 (Test_for_Output__beq, and_2_out[0]);

  // Notes on the sheet:
  //   set to 1 when inputs carry same value
endmodule

module _4_bit_memory (
  input  [3:0] MemoryAddress,
  input  [3:0] DataIn,
  input  Load_Store,
  input  Clock,
  input  CLR,
  output [3:0] DataOut
);

  wire controlled_inverter_1_out, controlled_inverter_2_out;

  assign controlled_inverter_1_out = Clock ? ~Load_Store : 1'bz;  // Controlled_Inverter controlled_inverter_1
  RAM #(.addrWidth(4), .dataWidth(4), .bus("separate")) ram_1 (
    .addr(MemoryAddress), .din(DataIn), .data(DataOut), .str(controlled_inverter_1_out), .clk(Clock),
    .ld(Load_Store), .clr(controlled_inverter_2_out));  // open: sel
  assign controlled_inverter_2_out = Load_Store ? ~CLR : 1'bz;  // Controlled_Inverter controlled_inverter_2
endmodule

module PC_Adder (
  input  [3:0] DataIn,
  input  CLK,
  input  CLR
);

  wire [3:0] adder_1_out, register_1_q;

  Register #(.width(4)) register_1 (.D(adder_1_out), .en(CLK), .Q(register_1_q), .clk(CLK), .clr(CLR));
  Adder #(.width(4)) adder_1 (.a(DataIn), .b(register_1_q), .out(adder_1_out));  // open: cin, cout
endmodule

module Q3_Store_in_Register (
  input  [3:0] Input_0,
  input  [3:0] Input_1,
  input  Clear,
  input  [2:0] Function,
  output beq
);

  wire Clock_Update_Button_out;
  wire [3:0] n4_bit_alu_1_result, Register_Storage_q;

  _4_Bit_ALU u_4_bit_alu_1 (
    .Input_0(Input_0), .Input_1(Input_1), .Function(Function), .Result(n4_bit_alu_1_result),
    .Test_for_Output__beq(beq));
  Button Clock_Update_Button (.out(Clock_Update_Button_out));
  Register #(.width(4)) Register_Storage (
    .D(n4_bit_alu_1_result), .Q(Register_Storage_q), .clk(Clock_Update_Button_out), .clr(Clear));  // open: en
  DotMatrix #(.inputtype("row"), .matrixcols(4), .matrixrows(1)) dotmatrix_1 (.row0(Register_Storage_q));
endmodule

module Q3_Store_in_Memory_RAM (
  input  [3:0] Input_0,
  input  [3:0] Input_1,
  input  [2:0] Function,
  input  Load,
  input  Reset,
  input  Control,
  input  Clear,
  input  Clock_Control,
  output beq
);

  wire clock_1_out, Clock_Button_out, controlled_buffer_1_out, controlled_buffer_2_out;
  wire [3:0] n4_bit_alu_1_result;
  wire [6:0] bit_extender_1_out, ram_1_data;
  wire [7:0] counter_1_q;

  _4_Bit_ALU u_4_bit_alu_1 (
    .Input_0(Input_0), .Input_1(Input_1), .Function(Function), .Result(n4_bit_alu_1_result),
    .Test_for_Output__beq(beq));
  assign controlled_buffer_1_out = Clock_Control ? clock_1_out : 1'bz;  // Controlled_Buffer controlled_buffer_1
  Clock clock_1 (.out(clock_1_out));
  assign bit_extender_1_out = {{3{1'b1}}, n4_bit_alu_1_result};  // Bit_Extender bit_extender_1
  Counter counter_1 (
    .load(Load), .Q(counter_1_q), .clk(controlled_buffer_1_out), .clr(Reset));  // open: D, count, carry
  RAM #(.dataWidth(7), .bus("separate")) ram_1 (
    .addr(counter_1_q), .din(bit_extender_1_out), .data(ram_1_data), .clk(controlled_buffer_1_out));  // open: str, sel, ld, clr
  assign controlled_buffer_2_out = Control ? clock_1_out : 1'bz;  // Controlled_Buffer controlled_buffer_2
  TTY tty_1 (.data(ram_1_data), .clk(controlled_buffer_2_out), .we(Clock_Button_out), .clr(Clear));
  Button Clock_Button (.out(Clock_Button_out));
endmodule

module Q3_Store_in_Memory_ROM (
  input  [3:0] Input_0,
  input  [3:0] Input_1,
  input  [2:0] Function,
  input  Clear,
  output beq
);

  wire clock_1_out;
  wire [3:0] n4_bit_alu_1_result, rom_1_data;
  wire [6:0] bit_extender_1_out;

  _4_Bit_ALU u_4_bit_alu_1 (
    .Input_0(Input_0), .Input_1(Input_1), .Function(Function), .Result(n4_bit_alu_1_result),
    .Test_for_Output__beq(beq));
  ROM #(.addrWidth(4), .dataWidth(4)) rom_1 (.addr(n4_bit_alu_1_result), .data(rom_1_data));  // open: sel
  Clock clock_1 (.out(clock_1_out));
  assign bit_extender_1_out = {{3{1'b1}}, rom_1_data};  // Bit_Extender bit_extender_1
  TTY tty_1 (.data(bit_extender_1_out), .clk(clock_1_out), .clr(Clear));  // open: we

  // Notes on the sheet:
  //   contents of rom_1 (hex, n*v repeats v):
  //   0 f 4*0 a 4*0 a
endmodule

module Q4_8_bit_bus (
  input  [7:0] Input_0,
  input  [7:0] Input_1,
  input  [2:0] Function,
  output [7:0] Result,
  output Test_for_Output__beq
);

  wire [7:0] adder_1_out, and_1_out, and_2_out, divider_1_out, multiplier_1_out, odd_parity_1_out, or_1_out,
       shifter_1_out, subtractor_1_out;

  Adder adder_1 (.a(Input_0), .b(Input_1), .out(adder_1_out));  // open: cin, cout
  Subtractor subtractor_1 (.a(Input_0), .b(Input_1), .out(subtractor_1_out));  // open: bin, bout
  assign or_1_out = Input_0 | Input_1;  // OR_Gate or_1, 8 bits wide
  assign and_1_out = Input_0 & Input_1;  // AND_Gate and_1, 8 bits wide
  Multiplier multiplier_1 (.a(Input_0), .b(Input_1), .out(multiplier_1_out));  // open: cin, cout
  Divider divider_1 (.a(Input_0), .b(Input_1), .out(divider_1_out));  // open: upper, rem
  Shifter shifter_1 (.in(Input_0), .\dist (Input_1[2:0]), .out(shifter_1_out));
  assign odd_parity_1_out = Input_0 ^ Input_1;  // Odd_Parity odd_parity_1, 8 bits wide
  Multiplexer #(.select(3), .width(8)) multiplexer_1 (
    .in0(adder_1_out), .in1(subtractor_1_out), .in2(or_1_out), .in3(and_1_out), .in4(multiplier_1_out),
    .in5(divider_1_out), .in6(shifter_1_out), .in7(odd_parity_1_out), .out(Result), .sel(Function));  // open: en
  assign and_2_out = subtractor_1_out & {8{1'b1}};  // AND_Gate and_2, 8 bits wide
  not not_1 (Test_for_Output__beq, and_2_out[0]);
endmodule
