// Logisim project Full_ALU.circ as structural Verilog
module Shifter_Circuit (
  input  D3,
  input  D2,
  input  D1,
  input  D0,
  input  Control,
  output out_6,
  output out_7,
  output out_8,
  output out_9
);

  wire and_1_out, and_3_out, and_4_out, and_6_out, not_1_out;

  not not_1 (not_1_out, Control);
  and and_1 (and_1_out, Control, D3);
  and and_2 (out_6, not_1_out, D2);
  and and_3 (and_3_out, D2, Control);
  or or_1 (out_7, and_1_out, and_4_out);
  and and_4 (and_4_out, not_1_out, D1);
  and and_5 (out_9, D1, Control);
  or or_2 (out_8, and_3_out, and_6_out);
  and and_6 (and_6_out, D0, not_1_out);

  // Notes on the sheet:
  //   Control = 1: shift right
  //   Control = 0: shift left
endmodule
