// Logisim project HW01.circ as structural Verilog: 8 circuits, main circuit main
module main (
  input  A4,
  input  A0,
  input  A7,
  input  A6,
  input  A5,
  input  A3,
  input  A2,
  input  A1,
  input  B7,
  input  B6,
  input  B5,
  input  B4,
  input  B3,
  input  B2,
  input  B1,
  input  B0,
  input  Carry_In,
  output S6,
  output S4,
  output S2,
  output S0,
  output S7,
  output S5,
  output S3,
  output S1,
  output Carry_Out
);

  _8bit_Adder u_8bit_adder_1 (
    .A4(A4), .A0(A0), .Carry_Out(Carry_Out), .B7(B7), .A7(A7), .B6(B6), .A6(A6), .B5(B5), .A5(A5), .B4(B4),
    .B3(B3), .A3(A3), .B2(B2), .A2(A2), .B1(B1), .A1(A1), .B0(B0), .S7(S7), .S6(S6), .S5(S5), .S4(S4),
    .S3(S3), .S2(S2), .S1(S1), .S0(S0), .Carry_In(Carry_In));

  // Notes on the sheet:
  //   A0-A7 represent 8 bits from input A.
  //   B0-B7 represent 8 bits from input B
  //   S0-S7 represent the 8-bit sum output
endmodule

module XOR (
  input  Input_A,
  input  Input_B,
  output Output
);

  wire AND_2_out, AND_out, Not_Gate_2_out, Not_Gate_out;

  not Not_Gate (Not_Gate_out, Input_A);
  not Not_Gate_2 (Not_Gate_2_out, Input_B);
  and AND (AND_out, Not_Gate_out, Input_B);
  and AND_2 (AND_2_out, Input_A, Not_Gate_2_out);
  or OR (Output, AND_out, AND_2_out);
endmodule

module Half_Adder (
  input  Input_A,
  input  Input_B,
  output Sum,
  output Carry_Out
);

  XOR xor_1 (.Input_A(Input_A), .Input_B(Input_B), .Output(Sum));
  and AND (Carry_Out, Input_A, Input_B);
endmodule

module Full_Adder (
  input  Carry_In,
  input  Input_A,
  input  Input_B,
  output Sum,
  output Carry_Out
);

  wire AND_2_out, AND_out, xor_1_output;

  XOR xor_1 (.Input_A(Input_A), .Input_B(Input_B), .Output(xor_1_output));
  and AND (AND_out, Input_A, Input_B);
  XOR xor_2 (.Input_A(Carry_In), .Input_B(xor_1_output), .Output(Sum));
  and AND_2 (AND_2_out, Carry_In, xor_1_output);
  or OR (Carry_Out, AND_2_out, AND_out);
endmodule

module Ripple_Adder (
  input  Carry_in,
  input  A0,
  input  B0,
  input  A1,
  input  B1,
  input  A2,
  input  B2,
  input  A3,
  input  B3,
  output S0,
  output S1,
  output S2,
  output S3,
  output Carry_Out
);

  wire full_adder_1_carry_out, full_adder_2_carry_out, full_adder_3_carry_out;

  Full_Adder full_adder_1 (
    .Carry_In(Carry_in), .Input_A(A0), .Input_B(B0), .Sum(S0), .Carry_Out(full_adder_1_carry_out));
  Full_Adder full_adder_2 (
    .Carry_In(full_adder_1_carry_out), .Input_A(A1), .Input_B(B1), .Sum(S1),
    .Carry_Out(full_adder_2_carry_out));
  Full_Adder full_adder_3 (
    .Carry_In(full_adder_2_carry_out), .Input_A(A2), .Input_B(B2), .Sum(S2),
    .Carry_Out(full_adder_3_carry_out));
  Full_Adder full_adder_4 (
    .Carry_In(full_adder_3_carry_out), .Input_A(A3), .Input_B(B3), .Sum(S3), .Carry_Out(Carry_Out));
endmodule

// 8-bit Adder
module _8bit_Adder (
  input  A4,
  input  A0,
  input  A7,
  input  A6,
  input  A5,
  input  A3,
  input  A2,
  input  A1,
  input  B7,
  input  B6,
  input  B5,
  input  B4,
  input  B3,
  input  B2,
  input  B1,
  input  B0,
  input  Carry_In,
  output Carry_Out,
  output S7,
  output S5,
  output S3,
  output S1,
  output S6,
  output S4,
  output S2,
  output S0
);

  wire ripple_adder_2_carry_out;

  Ripple_Adder ripple_adder_1 (
    .A0(A4), .Carry_in(ripple_adder_2_carry_out), .S0(S4), .S1(S5), .S2(S6), .S3(S7), .B0(B4), .A1(A5),
    .B1(B5), .A2(A6), .B2(B6), .A3(A7), .B3(B7), .Carry_Out(Carry_Out));
  Ripple_Adder ripple_adder_2 (
    .A0(A0), .Carry_in(Carry_In), .S0(S0), .S1(S1), .S2(S2), .S3(S3), .B0(B0), .A1(A1), .B1(B1), .A2(A2),
    .B2(B2), .A3(A3), .B3(B3), .Carry_Out(ripple_adder_2_carry_out));
endmodule

module Shifter (
  input  D3,
  input  D2,
  input  D1,
  input  D0,
  input  Control,
  output out_6,
  output out_7,
  output out_8,
  output out_9
);

  wire and_1_out, and_3_out, and_4_out, and_6_out, not_1_out;

  not not_1 (not_1_out, Control);
  and and_1 (and_1_out, Control, D3);
  and and_2 (out_6, not_1_out, D2);
  and and_3 (and_3_out, D2, Control);
  or or_1 (out_7, and_1_out, and_4_out);
  and and_4 (and_4_out, not_1_out, D1);
  and and_5 (out_9, D1, Control);
  or or_2 (out_8, and_3_out, and_6_out);
  and and_6 (and_6_out, D0, not_1_out);

  // Notes on the sheet:
  //   Control = 0: shift left
  //   Control = 1: shift right
endmodule

module ALU (
  input  Select,
  input  [7:0] in_2
);

  wire adder_1_cout, undriven_5;
  wire [7:0] adder_1_out, undriven, undriven_2, undriven_3, undriven_4;

  Adder adder_1 (.a(undriven), .b(undriven_2), .out(adder_1_out), .cin(undriven_5), .cout(adder_1_cout));
  Multiplier multiplier_1 (.a(in_2), .b(undriven_3), .cin(undriven_4));  // open: out, cout

  // Notes on the sheet:
  //   2 8-bit numbers
endmodule
